# Fritzing sketch volcano_skirt (saved by Fritzing 0.9.2b)

parts:
  FLORA1 = Adafruit_Flora
  U = Neopixel Strip -- White (30/m) [part_number=24]
  DL = Neopixel Strip -- White (30/m) [part_number=36]
  DR = Neopixel Strip -- White (30/m) [part_number=33]
  D = Neopixel Strip -- White (30/m) [part_number=27]
  UR = Neopixel Strip -- White (30/m) [part_number=36]
  VCC1 = 4 x AAA Battery Mount
  UL = Neopixel Strip -- White (30/m) [part_number=33]

nets:
  GND: FLORA1.connector1, U.GND, UR.GND
  N1: FLORA1.connector2, D.Din
  GND_2: FLORA1.connector7, DR.GND, D.GND
  N2: FLORA1.connector10, DR.Din, UL.Din
  GND_3: FLORA1.connector11, DL.GND, VCC1.-, UL.GND
  N3: FLORA1.connector12, DL.Din, UR.Din
  N4: FLORA1.connector13, U.Din
  +5V: U.+5V, DL.+5V, DR.+5V, D.+5V, UR.+5V, VCC1.+, UL.+5V

custom parts:
  Neopixel Strip -- White (30/m): These NeoPixel strips have 30 digitally-addressable pixel LEDs per meter and are very affordable and are only 12.5 mm wide, 10 mm if you remove the strip from the casing.
